// Logisim project PC_IM_32Bit.circ as structural Verilog: 1 circuit, main circuit main
module main (
  input  reset
);

  wire clock_out;
  wire [31:0] adder_1_out, PC_Register_q, rom_1_data;

  Register #(.width(32)) PC_Register (.D(adder_1_out), .en(1'b1), .Q(PC_Register_q), .clk(clock_out), .clr(reset));
  Clock clock (.out(clock_out));
  Adder #(.width(32)) adder_1 (.a(PC_Register_q), .b(32'h4), .out(adder_1_out));  // open: cin, cout
  ROM #(.addrWidth(4), .dataWidth(32)) rom_1 (.addr(PC_Register_q[5:2]), .data(rom_1_data), .sel(1'b1));
  // Probe on rom_1_data

  // Notes on the sheet:
  //          offset
  //     ADDER
  //              ROM
  //   contents of rom_1 (hex, n*v repeats v):
  //   500093 a00113 2081b3 40208233
endmodule
